# Fritzing sketch Connector_Shield_Schematic (saved by Fritzing 1.0.2b)
perfboards: 1

parts:
  NUCLEO-F411RE = STM32 Nucleo boards  # not connected
  J2 = female pin header, 19 pins [form="♀ (female)"]  # not connected
  J3 = female pin header, 19 pins [form="♀ (female)"]
  J4 = female pin header, 19 pins [form="♀ (female)"]
  J5 = female pin header, 19 pins [form="♀ (female)"]  # not connected
  7_5V_DC = 2.1mm DC Barrel Jack
  U1 = JST-XH-6A  # not connected
  U2 = JST XH 3A Male [chip_label=? package=THT]  # not connected
  U3 = JST XH 3A Male [chip_label=? package=THT]  # not connected
  UART = molex pin header, 6 pins [form=molex]
  X_Servo = molex pin header, 3 pins [form=molex]
  ADXL345 = molex pin header, 8 pins [form=molex]
  Y_Servo = molex pin header, 3 pins [form=molex]
  U4 = JST-XH-8A  # not connected

nets:
  N1: J3.pin11, UART.pin5
  N2: J3.pin13, ADXL345.pin6
  N3: J3.pin14, ADXL345.pin3
  N4: J3.pin15, ADXL345.pin2
  N5: J3.pin16, ADXL345.pin1
  N6: J3.pin17, UART.pin4
  N7: J4.pin3, UART.pin3
  N8: J4.pin8, ADXL345.pin7
  N9: J4.pin14, X_Servo.pin3
  N10: J4.pin15, Y_Servo.pin3
  N11: 7_5V_DC.center, Y_Servo.pin2
  N12: 7_5V_DC.switch, X_Servo.pin1, ADXL345.pin8, Y_Servo.pin1

custom parts:
  2.1mm DC Barrel Jack: 2.1mm DC Barrel Jack with Thru-Hole Connectors (breadboardable)
  JST-XH-6A: JST XH 6A (2.54)
  JST XH 3A Male: 2.54 Mm JST "XH" connector
  JST-XH-8A: JST XH 8A (2.54)
